// Logisim project surprise_processor.circ as structural Verilog
module ALU (
  input  [2:0] F,
  input  [31:0] B,
  input  [31:0] A,
  output out_4,
  output [31:0] Y
);

  wire [31:0] adder_1_out, and_1_out, bit_extender_1_out, multiplexer_1_out, not_1_out, or_1_out;

  Multiplexer #(.width(32)) multiplexer_1 (.in0(B), .in1(not_1_out), .out(multiplexer_1_out), .sel(F[2]));
  assign not_1_out = ~B;  // NOT_Gate not_1, 32 bits wide
  Adder #(.width(32)) adder_1 (.a(multiplexer_1_out), .b(A), .out(adder_1_out), .cin(F[2]));  // open: cout
  assign and_1_out = multiplexer_1_out & A;  // AND_Gate and_1, 32 bits wide
  assign or_1_out = multiplexer_1_out | A;  // OR_Gate or_1, 32 bits wide
  assign bit_extender_1_out = {{31{1'b0}}, adder_1_out[0]};  // Bit_Extender bit_extender_1
  Multiplexer #(.select(2), .width(32)) multiplexer_2 (
    .in0(and_1_out), .in1(or_1_out), .in2(adder_1_out), .in3(bit_extender_1_out), .out(Y), .sel(F[1:0]));
  Comparator #(.mode("unsigned"), .width(32)) comparator_1 (.a({32{1'b0}}), .b(Y), .eq(out_4));  // open: gt, lt
endmodule

module Datapath (
  input  OnOff,
  input  [7:0] in_2,
  input  Clear,
  output [31:0] Instruction,
  output [7:0] out_5,
  output [31:0] The_Output,
  output [31:0] V0Output
);

  wire alu_1_out_4, and_1_out, clock_1_out, controlunit_1_alusrc, controlunit_1_branch, controlunit_1_regdst,
       controlunit_1_regwrite, not_1_out;
  wire [2:0] controlunit_1_alucontrol;
  wire [4:0] multiplexer_3_out;
  wire [7:0] adder_1_out, adder_2_out, bit_extender_1_out, controlled_buffer_1_out, multiplexer_1_out,
       register_1_q, shifter_2_out;
  wire [31:0] multiplexer_2_out, registerfile_1_rd1, registerfile_1_rd2;
  wire [31:8] bit_extender_1_out_2;

  not not_1 (not_1_out, OnOff);
  assign controlled_buffer_1_out = OnOff ? in_2 : 8'bz;  // Controlled_Buffer controlled_buffer_1
  Clock clock_1 (.out(clock_1_out));
  assign controlled_buffer_1_out = not_1_out ? multiplexer_1_out : 8'bz;  // Controlled_Buffer controlled_buffer_2
  Register register_1 (.D(controlled_buffer_1_out), .Q(register_1_q), .clk(clock_1_out), .clr(Clear));  // open: en
  Shifter #(.shift("lr")) shifter_1 (.in(register_1_q), .\dist (3'b010), .out(out_5));
  Multiplexer #(.width(8)) multiplexer_1 (
    .in0(adder_1_out), .in1(adder_2_out), .out(multiplexer_1_out), .sel(and_1_out));
  Adder adder_1 (.a(register_1_q), .b(8'h4), .out(adder_1_out));  // open: cin, cout
  ROM #(.dataWidth(32)) rom_1 (.addr(out_5), .data(Instruction));
  RegisterFile registerfile_1 (
    .V0(V0Output), .RD1(registerfile_1_rd1), .RD2(registerfile_1_rd2), .WD3(The_Output), .CLK(clock_1_out),
    .A3(multiplexer_3_out), .A1(Instruction[25:21]), .A2(Instruction[20:16]), .WE3(controlunit_1_regwrite));
  assign {bit_extender_1_out_2, bit_extender_1_out} = {{16{Instruction[15]}}, Instruction[15:0]};  // Bit_Extender bit_extender_1
  ControlUnit controlunit_1 (
    .RegWrite(controlunit_1_regwrite), .ALUControl(controlunit_1_alucontrol), .Branch(controlunit_1_branch),
    .RegDst(controlunit_1_regdst), .ALUSrc(controlunit_1_alusrc), .Instruction(Instruction));
  Multiplexer #(.width(32)) multiplexer_2 (
    .in0(registerfile_1_rd2), .in1({bit_extender_1_out_2, bit_extender_1_out}), .out(multiplexer_2_out),
    .sel(controlunit_1_alusrc));
  Multiplexer #(.width(5)) multiplexer_3 (
    .in0(Instruction[20:16]), .in1(Instruction[15:11]), .out(multiplexer_3_out), .sel(controlunit_1_regdst));
  Shifter shifter_2 (.in(bit_extender_1_out), .\dist (3'b010), .out(shifter_2_out));
  ALU alu_1 (
    .Y(The_Output), .out_4(alu_1_out_4), .B(multiplexer_2_out), .A(registerfile_1_rd1),
    .F(controlunit_1_alucontrol));
  Adder adder_2 (.a(shifter_2_out), .b(adder_1_out), .out(adder_2_out));  // open: cin, cout
  and and_1 (and_1_out, controlunit_1_branch, alu_1_out_4);

  // Notes on the sheet:
  //   contents of rom_1 (hex, n*v repeats v):
  //   20840005 2085ffff c53020 20020001 1080000f 20 10a0000d 20 1020 50820 10200005 20 441020 2021ffff
  //   1000fffb 20 20a5ffff 22020 1000fff1 20 1000ffff 20
endmodule

module Tests (
  output [31:0] Y,
  output [7:0] out_2,
  output [7:0] out_3,
  output [2:0] out_4
);

  BitSelector #(.group(8), .width(32)) bitselector_1 (.in(32'h300), .out(out_2), .sel(2'b10));
  BitSelector #(.group(8), .width(32)) bitselector_2 (.in(32'h12356789), .out(out_3), .sel(2'b01));
  BitSelector #(.group(3)) bitselector_3 (.in(out_3), .out(out_4), .sel(2'b00));

  assign Y = 32'hf4010207;

  // Notes on the sheet:
  //   binary values in Logisim. Convince yourself how the bits are displayed.
  //   Example 2: The bit selector is configured to have 32  
  //   bit group #1 (starting at index 0) is selected for the output.
  //   That is, the 8 bits 0x67 at bit indices 15..8  are sent to the output.
  //   Example 3: Now, assume that you want to extract 3 bits at   
  //   Example 1: A simple example that illustrates how 32-bit values are displayed as 
  //   input bits and 8 output bits. The parameter constant is 1, which means that   
  //   bit indices 10..8. This can be accoplished by putting two bit selecotrs in series.
endmodule

module RegisterFile (
  input  CLK,
  input  [4:0] A1,
  input  [31:0] WD3,
  input  [4:0] A2,
  input  WE3,
  input  [4:0] A3,
  output [31:0] RD1,
  output [31:0] RD2,
  output [31:0] V0
);

  wire and_1_out, and_2_out, and_3_out, and_4_out, and_5_out, and_6_out, and_7_out, and_8_out,
       decoder_1_out0, decoder_1_out1, decoder_1_out2, decoder_1_out3, decoder_1_out4, decoder_1_out5,
       decoder_1_out6, decoder_1_out7;
  wire [31:0] register_1_q, register_2_q, register_4_q, register_5_q, register_6_q, register_7_q,
       register_8_q;

  Decoder #(.select(3)) decoder_1 (
    .out0(decoder_1_out0), .out1(decoder_1_out1), .out2(decoder_1_out2), .out3(decoder_1_out3),
    .out4(decoder_1_out4), .out5(decoder_1_out5), .out6(decoder_1_out6), .out7(decoder_1_out7), .sel(A3[2:0]));  // open: en
  and and_1 (and_1_out, WE3, decoder_1_out0);
  and and_2 (and_2_out, WE3, decoder_1_out1);
  and and_3 (and_3_out, WE3, decoder_1_out2);
  and and_4 (and_4_out, WE3, decoder_1_out3);
  and and_5 (and_5_out, WE3, decoder_1_out4);
  and and_6 (and_6_out, WE3, decoder_1_out5);
  and and_7 (and_7_out, WE3, decoder_1_out6);
  and and_8 (and_8_out, WE3, decoder_1_out7);
  Register #(.width(32)) register_1 (.D(WD3), .en(and_1_out), .clk(CLK), .Q(register_1_q), .clr(1'b0));
  Register #(.width(32)) register_2 (.D(WD3), .en(and_2_out), .clk(CLK), .Q(register_2_q), .clr(1'b0));
  Register #(.width(32)) register_3 (.D(WD3), .en(and_3_out), .clk(CLK), .Q(V0), .clr(1'b0));
  Register #(.width(32)) register_4 (.D(WD3), .en(and_4_out), .clk(CLK), .Q(register_4_q), .clr(1'b0));
  Register #(.width(32)) register_5 (.D(WD3), .en(and_5_out), .clk(CLK), .Q(register_5_q), .clr(1'b0));
  Register #(.width(32)) register_6 (.D(WD3), .en(and_6_out), .clk(CLK), .Q(register_6_q), .clr(1'b0));
  Register #(.width(32)) register_7 (.D(WD3), .en(and_7_out), .clk(CLK), .Q(register_7_q), .clr(1'b0));
  Register #(.width(32)) register_8 (.D(WD3), .en(and_8_out), .clk(CLK), .Q(register_8_q), .clr(1'b0));
  Multiplexer #(.select(3), .width(32)) multiplexer_1 (
    .in0(register_1_q), .in1(register_2_q), .in2(V0), .in3(register_4_q), .in4(register_5_q),
    .in5(register_6_q), .in6(register_7_q), .in7(register_8_q), .out(RD1), .sel(A1[2:0]));
  Multiplexer #(.select(3), .width(32)) multiplexer_2 (
    .in0(register_1_q), .in1(register_2_q), .in2(V0), .in3(register_4_q), .in4(register_5_q),
    .in5(register_6_q), .in6(register_7_q), .in7(register_8_q), .out(RD2), .sel(A2[2:0]));
endmodule

module ControlUnit (
  input  [31:0] Instruction,
  output RegDst,
  output RegWrite,
  output ALUSrc,
  output [2:0] ALUControl,
  output Branch
);

  wire comparator_1_eq, comparator_2_eq, not_1_out, not_2_out;
  wire [5:0] bitselector_1_out;
  wire [31:0] shifter_1_out;

  Shifter #(.shift("lr"), .width(32)) shifter_1 (.in(Instruction), .\dist (5'b11010), .out(shifter_1_out));
  BitSelector #(.group(6), .width(32)) bitselector_1 (.in(shifter_1_out), .out(bitselector_1_out), .sel(3'b000));
  Comparator #(.mode("unsigned"), .width(6)) comparator_1 (
    .a(bitselector_1_out), .b(6'b001000), .eq(comparator_1_eq));  // open: gt, lt
  Comparator #(.mode("unsigned"), .width(6)) comparator_2 (
    .a(bitselector_1_out), .b({6{1'b0}}), .eq(comparator_2_eq));  // open: gt, lt
  Comparator #(.mode("unsigned"), .width(6)) comparator_3 (
    .a(bitselector_1_out), .b(6'b000100), .eq(Branch));  // open: gt, lt
  not not_1 (not_1_out, Branch);
  not not_2 (not_2_out, Branch);
  and and_1 (RegDst, not_1_out, comparator_2_eq);
  or or_1 (RegWrite, comparator_1_eq, comparator_2_eq);
  Multiplexer #(.width(3)) multiplexer_1 (.in0(3'b010), .in1(3'b110), .out(ALUControl), .sel(Branch));
  and and_2 (ALUSrc, comparator_1_eq, not_2_out);
endmodule
